# Fritzing sketch Schema elettrico (saved by Fritzing 0.9.3b)
breadboards: 1

parts:
  U1 = ESP8266 WiFi Module [part_number=ESP8266]
  Componente1 = Arduino Uno (Rev3)
  V1 = DC Power [voltage=6]
  Indice = Basic Servo
  Anulare = Basic Servo
  Mignolo = Basic Servo
  Medio = Basic Servo
  Pollice = Basic Servo
  Polso = Basic Servo

nets:
  N1: U1.RXD, Componente1.D0/RX
  VCC: U1.VCC, Componente1.5V
  N2: U1.GPIO_0, Componente1.D2
  GND: U1.GND, Componente1.GND, V1.V-, Anulare.gnd, Mignolo.gnd, Polso.gnd
  N3: U1.TXD, Componente1.D1/TX
  N4: U1.REST, Componente1.RESET
  N5: Componente1.D8, Polso.pulse
  N6: Componente1.D3_PWM, Pollice.pulse
  N7: Componente1.D4, Indice.pulse
  N8: Componente1.D5_PWM, Medio.pulse
  N9: Componente1.D6_PWM, Anulare.pulse
  N10: Componente1.D7, Mignolo.pulse
  VCC_2: Componente1.VIN, V1.V+, Indice.vcc, Anulare.vcc, Mignolo.vcc, Medio.vcc, Pollice.vcc, Polso.vcc
  GND_2: Indice.gnd, Medio.gnd, Pollice.gnd
